// Logisim project MUX_and_Decoder.circ as structural Verilog: 1 circuit, main circuit main
module main (
  input  A,
  input  B,
  input  C,
  input  D,
  input  E,
  input  F,
  output G,
  output H
);

  wire decoder_1_out0, decoder_1_out1, decoder_1_out3, decoder_2_out2, not_1_out, not_2_out, not_3_out,
       not_4_out, not_5_out, not_6_out, not_7_out;

  not not_1 (not_1_out, C);
  Multiplexer #(.select(2)) multiplexer_1 (.in0(C), .in1(not_1_out), .in2(not_2_out), .in3(C), .out(G), .sel({A, B}));
  not not_2 (not_2_out, C);
  not not_3 (not_3_out, D);
  Decoder #(.select(2)) decoder_1 (
    .out0(decoder_1_out0), .out1(decoder_1_out1), .out3(decoder_1_out3), .sel({E, F}), .en(not_3_out));  // open: out2
  not not_4 (not_4_out, decoder_1_out0);
  not not_5 (not_5_out, decoder_1_out1);
  Decoder #(.select(2)) decoder_2 (.out2(decoder_2_out2), .sel({E, F}), .en(D));  // open: out0, out1, out3
  not not_6 (not_6_out, decoder_1_out3);
  not not_7 (not_7_out, decoder_2_out2);
  nand nand_1 (H, not_4_out, not_5_out, not_7_out, not_6_out);
endmodule
